# Fritzing sketch burglar-alarm-circuit (saved by Fritzing 0.9.3b)
breadboards: 1

parts:
  Part1 = Adafruit T-Cobbler Plus [part_number="Adafruit #1989 and #2028"]
  LCM1602_IIC1 = LCM1602 IIC [part_number="LCM1602 IIC" chip_label="LCM1602 IIC" package="DIP (Dual Inline) [THT]"]
  LCD1 = LCD screen
  SG1 = Buzzer 12mm [package=buzzer-12mm-ns]
  Q1 = NPN-Transistor [package="TO92 [THT]"]
  Keypad4x1 = Keypad Membran 4x4
  R1 = Resistor [tolerance=±5% resistance=1k package=THT]
  hc-sr1 = hc-sr04
  R2 = Resistor [tolerance=±5% resistance=1k package=THT]
  R3 = Resistor [tolerance=±5% resistance=1k package=THT]
  R4 = Resistor [tolerance=±5% resistance=1k package=THT]
  R5 = Resistor [tolerance=±5% resistance=10k package=THT]
  R6 = Resistor [tolerance=±5% resistance=10k package=THT]
  R9 = Resistor [tolerance=±5% resistance=10k package=THT]  # not connected
  R10 = Resistor [tolerance=±5% resistance=10k package=THT]

nets:
  N1: Part1.SDA, LCM1602_IIC1.SDA
  N2: Part1.SCL, LCM1602_IIC1.SCL
  GND: Part1.GND, LCM1602_IIC1.GND, Q1.E, hc-sr1.GND
  N3: Part1.GPIO27, Keypad4x1.Pin7
  N4: Part1.GPIO22, Keypad4x1.Pin5
  N5: Part1.+3.3V_2, R5.Pin_1, R6.Pin_1, R10.Pin_1
  N6: Part1.MOSI, Keypad4x1.Pin6
  N7: Part1.GPIO5, R1.Pin_0
  N8: Part1.GPIO26, R2.Pin_1
  VCC: Part1.+5V, LCM1602_IIC1.VCC, SG1.2, hc-sr1.VCC
  N9: Part1.GPIO18, Keypad4x1.Pin1, Keypad4x1.Pin8, R5.Pin_0
  N10: Part1.GPIO23, Keypad4x1.Pin2, R6.Pin_0
  N11: Part1.GPIO24, Keypad4x1.Pin3
  N12: Part1.GPIO25, Keypad4x1.Pin4, R10.Pin_0
  N13: Part1.GPIO21, hc-sr1.Trig
  N14: LCM1602_IIC1.VSS, LCD1.LED-
  N15: LCM1602_IIC1.VDD, LCD1.LED+
  N16: LCM1602_IIC1.V0, LCD1.DB7
  N17: LCM1602_IIC1.RS, LCD1.DB6
  N18: LCM1602_IIC1.RW, LCD1.DB5
  N19: LCM1602_IIC1.E, LCD1.DB4
  N20: LCM1602_IIC1.D0, LCD1.DB3
  N21: LCM1602_IIC1.D1, LCD1.DB2
  N22: LCM1602_IIC1.D2, LCD1.DB1
  N23: LCM1602_IIC1.D3, LCD1.DB0
  N24: LCM1602_IIC1.D4, LCD1.E
  N25: LCM1602_IIC1.D5, LCD1.R/W
  N26: LCM1602_IIC1.D6, LCD1.RS
  N27: LCM1602_IIC1.D7, LCD1.V0
  N28: LCM1602_IIC1.A, LCD1.VDD
  N29: LCM1602_IIC1.K, LCD1.VSS
  N30: LCM1602_IIC1.LED_A, LCM1602_IIC1.LED_B
  N31: SG1.1, Q1.C
  N32: Q1.B, R1.Pin_1
  N33: hc-sr1.Echo, R3.Pin_0, R4.Pin_1
  N34: R2.Pin_0, R3.Pin_1

custom parts:
  Adafruit T-Cobbler Plus: The Raspberry Pi has landed on the Maker World like a 40-GPIO pinned, quad-USB ported, credit card sized bomb of DIY joy. And while you can use most of our great Model B accessories by hooking up our downgrade cable, its probably a good time to upgrade your set up and accessorize using all of the 40 pins. That's why we now carry the Assembled Adafruit Pi T-Cobbler Plus - Breakout + Cable for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
  LCM1602 IIC: I2C-Module to use a 1602 or 2004 LCD on with the wire.h libory Serial LCD Modul
  Keypad Membran 4x4: Membrane Keypad 4x4 Matrix
